# Fritzing sketch magic8ball (saved by Fritzing 0.9.4)
breadboards: 1

parts:
  Part1 = Arduino Uno (Rev3)
  R1 = Basic Flex Resistor
  R2 = Resistor [tolerance=±5% resistance=10k package=THT]
  U1 = LCD-16X2 [package=lcd-16x2]
  IC1 = SHIFT REGISTER [package=dil16]
  R3 = Trimmer Potentiometer [maximum_resistance=10kΩ package=THT]
  R4 = Resistor [tolerance=±5% resistance=220 package=THT]

nets:
  N1: Part1.A0, R1.Pin_2, R2.Pin_0
  N2: Part1.D9_PWM, IC1.RCK
  N3: Part1.D11_PWM/MOSI, IC1.SER
  N4: Part1.D13/SCK, IC1.SCK
  GND: Part1.GND, R1.pin_1, U1.VSS, U1.R_W, U1.K, IC1.GND, IC1.G, R3.leg1
  5V: Part1.5V, R2.Pin_1, U1.VDD, IC1.SCL, IC1.VCC, R3.leg2, R4.Pin_1
  N5: U1.VO, R3.wiper
  N6: U1.RS, IC1.QB
  N7: U1.E, IC1.QD
  N8: U1.DB4, IC1.QE
  N9: U1.DB5, IC1.QF
  N10: U1.DB6, IC1.QG
  N11: U1.DB7, IC1.QH
  N12: U1.A, R4.Pin_0
