# Fritzing sketch redo7a (saved by Fritzing 0.9.4)
breadboards: 1

parts:
  Part1 = Arduino Uno (Rev3)
  R1 = Photocell (LDR) [package=THT]
  R2 = Resistor [tolerance=±5% resistance=220 package=THT]
  U1 = TRANSISTOR_NPN_2 [package=to-92]
  R3 = Resistor [tolerance=±5% resistance=220 package=THT]
  D1 = Rectifier Diode [part_number=1N4001 package="300 mil [THT]"]
  M1 = DC Motor
  C1 = Electrolytic Capacitor [capacitance=1µF package="100 mil [THT, electrolytic]"]
  IC1 = Voltage Regulator [package=to220-igo]
  C2 = Tantalum Capacitor [capacitance="1 μF" package="C 6032 [SMD, tantalum]"]
  VCC1 = Battery block 9V

nets:
  N1: Part1.A0, R1.pin_1, R2.Pin_0
  N2: Part1.D3_PWM, R3.Pin_0
  N3: Part1.5V, R2.Pin_1
  N4: Part1.GND, R1.pin_0, U1.C, C1.-, IC1.IN, C2.-, VCC1.-
  N5: U1.B, R3.Pin_1
  N6: U1.E, D1.anode, M1.pin_2
  N7: D1.cathode, M1.pin_1, IC1.OUT, C2.+
  N8: C1.+, IC1.GND, VCC1.+
