# Fritzing sketch h-bridge sketch (saved by Fritzing 0.9.4)
breadboards: 1

parts:
  U1 = NJM2670 [package=so-24w]
  Part1 = Arduino Uno (Rev3)
  M1 = DC Motor
  VCC1 = Battery block 9V
  R1 = Photocell (LDR) [package=THT]
  R2 = Resistor [tolerance=±5% resistance=220 package=THT]

nets:
  N1: U1.NC, U1.OUTA1, U1.SENSEB, U1.VSB, Part1.D8, Part1.D7, Part1.GND, VCC1.-, R2.Pin_0
  N2: U1.INB1, VCC1.+
  N3: U1.ENABLEB, Part1.D9_PWM
  N4: U1.OUTB1, M1.pin_2
  N5: U1.OUTB2, M1.pin_1
  N6: U1.TSDARM, Part1.5V, R1.pin_1
  N7: Part1.A0, R1.pin_0, R2.Pin_1
